# Fritzing sketch arduinoclock (saved by Fritzing 0.9.8b)

parts:
  Bauteil1 = Arduino Nano (Rev3.0)
  DHT1 = DHT11 Humitidy and Temperature Sensor  # not connected
  PCB2 = RTC_DS1302_module
  LCM1602_IIC1 = LCM1602 IIC [part_number="LCM1602 IIC" chip_label="LCM1602 IIC" package="DIP (Dual Inline) [THT]"]
  LCD1 = LCD screen

nets:
  N1: Bauteil1.D4, PCB2.DAT
  N2: Bauteil1.D5, PCB2.RST
  N3: Bauteil1.D9, PCB2.CLK
  N4: Bauteil1.A5, LCM1602_IIC1.SCL
  N5: Bauteil1.A4, LCM1602_IIC1.SDA
  VSS: LCM1602_IIC1.VSS, LCD1.VSS
  VDD: LCM1602_IIC1.VDD, LCD1.VDD
  N6: LCM1602_IIC1.V0, LCD1.V0
  N7: LCM1602_IIC1.RS, LCD1.RS
  N8: LCM1602_IIC1.RW, LCD1.R/W
  N9: LCM1602_IIC1.E, LCD1.E
  N10: LCM1602_IIC1.D0, LCD1.DB0
  N11: LCM1602_IIC1.D1, LCD1.DB1
  N12: LCM1602_IIC1.D2, LCD1.DB2
  N13: LCM1602_IIC1.D3, LCD1.DB3
  N14: LCM1602_IIC1.D4, LCD1.DB4
  N15: LCM1602_IIC1.D5, LCD1.DB5
  N16: LCM1602_IIC1.D6, LCD1.DB6
  N17: LCM1602_IIC1.D7, LCD1.DB7
  N18: LCM1602_IIC1.A, LCD1.LED+
  N19: LCM1602_IIC1.K, LCD1.LED-
  N20: LCM1602_IIC1.LED_A, LCM1602_IIC1.LED_B

custom parts:
  DHT11 Humitidy and Temperature Sensor: DHT11 Humidity and Temperature Sensor
  RTC_DS1302_module: Arduino module DS1302 SPI Real Time Clock
  LCM1602 IIC: I2C-Module to use a 1602 or 2004 LCD on with the wire.h libory Serial LCD Modul
